// Digital circuit ALUDecoder.dig as structural Verilog
module ALUDecoder (
  input  [3:0] address,
  output [7:0] ALU_in
);

  wire [7:0] multiplexer_1_out, multiplexer_2_out;

  Multiplexer #(.Selector_Bits(3), .Bits(8)) multiplexer_1 (
    .sel(address[2:0]), .in_0({8{1'b0}}), .in_1(8'h51), .in_2(8'h70), .in_3(8'h2), .in_4(8'h43),
    .in_5(8'h33), .in_6(8'h4), .in_7(8'h6), .out(multiplexer_1_out));
  Multiplexer #(.Selector_Bits(3), .Bits(8)) multiplexer_2 (
    .sel(address[2:0]), .in_0(8'h8), .in_1(8'ha), .in_2(8'hc), .in_3(8'h30), .in_4(8'he), .in_5({8{1'b0}}),
    .in_6({8{1'b0}}), .in_7({8{1'b0}}), .out(multiplexer_2_out));
  Multiplexer #(.Bits(8)) multiplexer_3 (
    .sel(address[3]), .in_0(multiplexer_1_out), .in_1(multiplexer_2_out), .out(ALU_in));

  // Notes on the sheet:
  //   AND (x&y)
  //   SUB (x-y)
  //   MOD (x%y)
  //   XOR (x\^y)
  //   OR (x|y)
  //   NEG (-x)
  //   ABS (|x|)
  //   UNUSED
  //   NOT (~x)
  //   MULT (x*y)
  //   SQRT (\_/x)
  //   ADD (x+y)
  //   DIV (x/y)
  //   NOP (x)
endmodule
