// Digital circuit Abs16.dig as structural Verilog
module Abs16 (
  input  [15:0] in,
  output [15:0] out,
  output Sign
);

  wire [15:0] add16_1_p3, not_1_out, xor_1_out;

  assign not_1_out = ~xor_1_out;  // Not not_1, 16 bits wide
  assign xor_1_out = {16{in[15]}} ^ in;  // XOr xor_1, 16 bits wide
  assign out = ~add16_1_p3;  // Not not_2, 16 bits wide
  // Add16 add16_1: pin names not known; wires that end beside it: {16{in[15]}}, not_1_out, add16_1_p3

  assign Sign = in[15];
endmodule
