// Digital circuit Add16.dig as structural Verilog
module Add16 (
  input  [15:0] A,
  input  [15:0] B,
  output [15:0] out
);

  wire fulladder_1_p1, fulladder_1_p5, fulladder_2_p5, fulladder_3_p5, fulladder_5_p1, fulladder_5_p5,
       fulladder_6_p5, fulladder_7_p5, fulladder_9_p1, fulladder_9_p5, fulladder_10_p5, fulladder_11_p5,
       fulladder_13_p5, fulladder_14_p5, halfadder_1_p4;

  // FullAdder fulladder_1: pin names not known; wires that end beside it: fulladder_1_p1, A[12], B[12], out[12], fulladder_1_p5
  // FullAdder fulladder_2: pin names not known; wires that end beside it: fulladder_1_p5, A[13], B[13], out[13], fulladder_2_p5
  // FullAdder fulladder_3: pin names not known; wires that end beside it: fulladder_2_p5, A[14], B[14], out[14], fulladder_3_p5
  // FullAdder fulladder_4: pin names not known; wires that end beside it: fulladder_3_p5, A[15], B[15], out[15]
  // FullAdder fulladder_5: pin names not known; wires that end beside it: fulladder_5_p1, A[8], B[8], out[8], fulladder_5_p5
  // FullAdder fulladder_6: pin names not known; wires that end beside it: fulladder_5_p5, A[9], B[9], out[9], fulladder_6_p5
  // FullAdder fulladder_7: pin names not known; wires that end beside it: fulladder_6_p5, A[10], B[10], out[10], fulladder_7_p5
  // FullAdder fulladder_8: pin names not known; wires that end beside it: fulladder_7_p5, A[11], B[11], out[11], fulladder_1_p1
  // FullAdder fulladder_9: pin names not known; wires that end beside it: fulladder_9_p1, A[4], B[4], out[4], fulladder_9_p5
  // FullAdder fulladder_10: pin names not known; wires that end beside it: fulladder_9_p5, A[5], B[5], out[5], fulladder_10_p5
  // FullAdder fulladder_11: pin names not known; wires that end beside it: fulladder_10_p5, A[6], B[6], out[6], fulladder_11_p5
  // FullAdder fulladder_12: pin names not known; wires that end beside it: fulladder_11_p5, A[7], B[7], out[7], fulladder_5_p1
  // HalfAdder halfadder_1: pin names not known; wires that end beside it: A[0], B[0], out[0], halfadder_1_p4
  // FullAdder fulladder_13: pin names not known; wires that end beside it: halfadder_1_p4, A[1], B[1], out[1], fulladder_13_p5
  // FullAdder fulladder_14: pin names not known; wires that end beside it: fulladder_13_p5, A[2], B[2], out[2], fulladder_14_p5
  // FullAdder fulladder_15: pin names not known; wires that end beside it: fulladder_14_p5, A[3], B[3], out[3], fulladder_9_p1
endmodule
