// Digital circuit MultAdder.dig as structural Verilog
module MultAdder (
  input  S,
  input  y,
  input  C,
  input  x,
  output Sum,
  output Carry
);

  wire and_1_out;

  and and_1 (and_1_out, x, y);
  // FullAdder fulladder_1: pin names not known; wires that end beside it: S, and_1_out, C, Sum, Carry
endmodule
