// Digital circuit Sqrt16.dig as structural Verilog
module Sqrt16 (
  input  [15:0] x,
  output [15:0] Quotient
);

  wire controlledsubmultiplex_1_p2, controlledsubmultiplex_1_p5, controlledsubmultiplex_2_p5,
       controlledsubmultiplex_2_p6, controlledsubmultiplex_3_p2, controlledsubmultiplex_3_p5,
       controlledsubmultiplex_4_p5, controlledsubmultiplex_5_p5, controlledsubmultiplex_5_p6,
       controlledsubmultiplex_6_p2, controlledsubmultiplex_6_p5, controlledsubmultiplex_7_p5,
       controlledsubmultiplex_7_p6, controlledsubmultiplex_8_p5, controlledsubmultiplex_8_p6,
       controlledsubmultiplex_9_p2, controlledsubmultiplex_9_p5, controlledsubmultiplex_10_p5,
       controlledsubmultiplex_11_p1, controlledsubmultiplex_11_p5, controlledsubmultiplex_11_p6,
       controlledsubmultiplex_12_p5, controlledsubmultiplex_12_p6, controlledsubmultiplex_13_p2,
       controlledsubmultiplex_13_p5, controlledsubmultiplex_14_p5, controlledsubmultiplex_14_p6,
       controlledsubmultiplex_15_p5, controlledsubmultiplex_15_p6, controlledsubmultiplex_16_p5,
       controlledsubmultiplex_16_p6, controlledsubmultiplex_17_p2, controlledsubmultiplex_17_p5,
       controlledsubmultiplex_18_p5, controlledsubmultiplex_19_p5, controlledsubmultiplex_19_p6,
       controlledsubmultiplex_20_p5, controlledsubmultiplex_20_p6, controlledsubmultiplex_21_p5,
       controlledsubmultiplex_21_p6, controlledsubmultiplex_22_p2, controlledsubmultiplex_22_p5,
       controlledsubmultiplex_23_p5, controlledsubmultiplex_23_p6, controlledsubmultiplex_24_p5,
       controlledsubmultiplex_24_p6, controlledsubmultiplex_25_p5, controlledsubmultiplex_25_p6,
       controlledsubmultiplex_26_p5, controlledsubmultiplex_26_p6, controlledsubmultiplex_27_p2,
       controlledsubmultiplex_27_p5, controlledsubmultiplex_28_p5, controlledsubmultiplex_29_p1,
       controlledsubmultiplex_29_p5, controlledsubmultiplex_29_p6, controlledsubmultiplex_30_p5,
       controlledsubmultiplex_30_p6, controlledsubmultiplex_31_p5, controlledsubmultiplex_31_p6,
       controlledsubmultiplex_32_p5, controlledsubmultiplex_33_p5, controlledsubmultiplex_33_p6,
       controlledsubmultiplex_34_p5, controlledsubmultiplex_34_p6, controlledsubmultiplex_35_p5,
       controlledsubmultiplex_35_p6, controlledsubmultiplex_36_p5, controlledsubmultiplex_37_p5,
       controlledsubmultiplex_38_p5, controlledsubmultiplex_38_p6, controlledsubmultiplex_39_p5,
       controlledsubmultiplex_39_p6, controlledsubmultiplex_40_p5, controlledsubmultiplex_41_p5,
       controlledsubmultiplex_41_p6, controlledsubmultiplex_42_p5, controlledsubmultiplex_42_p6,
       controlledsubmultiplex_43_p5, controlledsubmultiplex_44_p5, controlledsubmultiplex_45_p1,
       controlledsubmultiplex_45_p5, controlledsubmultiplex_45_p6, controlledsubmultiplex_46_p5,
       controlledsubmultiplex_47_p5, controlledsubmultiplex_47_p6, controlledsubmultiplex_48_p5,
       controlledsubmultiplex_49_p5, controlledsubmultiplex_50_p5, controlledsubmultiplex_51_p5, not_2_out,
       not_8_out, not_13_out, not_15_out;

  // ControlledSubMultiplex controlledsubmultiplex_1: pin names not known; wires that end beside it: 1'b0, controlledsubmultiplex_1_p2, controlledsubmultiplex_1_p2, 1'b0, controlledsubmultiplex_1_p5
  not not_1 (Quotient[7], controlledsubmultiplex_1_p2);
  // ControlledSubMultiplex controlledsubmultiplex_2: pin names not known; wires that end beside it: 1'b0, controlledsubmultiplex_1_p5, controlledsubmultiplex_1_p2, x[15], controlledsubmultiplex_2_p5, controlledsubmultiplex_2_p6
  // ControlledSubMultiplex controlledsubmultiplex_3: pin names not known; wires that end beside it: 1'b0, controlledsubmultiplex_3_p2, controlledsubmultiplex_3_p2, controlledsubmultiplex_2_p5, controlledsubmultiplex_3_p5
  not not_2 (not_2_out, controlledsubmultiplex_1_p2);
  not not_3 (Quotient[6], controlledsubmultiplex_3_p2);
  // ControlledSubMultiplex controlledsubmultiplex_4: pin names not known; wires that end beside it: 1'b1, controlledsubmultiplex_2_p6, controlledsubmultiplex_1_p2, x[14], controlledsubmultiplex_4_p5, 1'b0
  // ControlledSubMultiplex controlledsubmultiplex_5: pin names not known; wires that end beside it: not_2_out, controlledsubmultiplex_3_p5, controlledsubmultiplex_3_p2, controlledsubmultiplex_4_p5, controlledsubmultiplex_5_p5, controlledsubmultiplex_5_p6
  // ControlledSubMultiplex controlledsubmultiplex_6: pin names not known; wires that end beside it: 1'b0, controlledsubmultiplex_6_p2, controlledsubmultiplex_6_p2, controlledsubmultiplex_5_p5, controlledsubmultiplex_6_p5
  not not_4 (Quotient[5], controlledsubmultiplex_6_p2);
  // ControlledSubMultiplex controlledsubmultiplex_7: pin names not known; wires that end beside it: 1'b0, controlledsubmultiplex_5_p6, controlledsubmultiplex_3_p2, x[13], controlledsubmultiplex_7_p5, controlledsubmultiplex_7_p6
  // ControlledSubMultiplex controlledsubmultiplex_8: pin names not known; wires that end beside it: not_2_out, controlledsubmultiplex_6_p5, controlledsubmultiplex_6_p2, controlledsubmultiplex_7_p5, controlledsubmultiplex_8_p5, controlledsubmultiplex_8_p6
  // ControlledSubMultiplex controlledsubmultiplex_9: pin names not known; wires that end beside it: 1'b0, controlledsubmultiplex_9_p2, controlledsubmultiplex_9_p2, controlledsubmultiplex_8_p5, controlledsubmultiplex_9_p5
  not not_5 (Quotient[4], controlledsubmultiplex_9_p2);
  // ControlledSubMultiplex controlledsubmultiplex_10: pin names not known; wires that end beside it: 1'b1, controlledsubmultiplex_7_p6, controlledsubmultiplex_3_p2, x[12], controlledsubmultiplex_10_p5, 1'b0
  // ControlledSubMultiplex controlledsubmultiplex_11: pin names not known; wires that end beside it: controlledsubmultiplex_11_p1, controlledsubmultiplex_8_p6, controlledsubmultiplex_6_p2, controlledsubmultiplex_10_p5, controlledsubmultiplex_11_p5, controlledsubmultiplex_11_p6
  not not_6 (controlledsubmultiplex_11_p1, controlledsubmultiplex_3_p2);
  // ControlledSubMultiplex controlledsubmultiplex_12: pin names not known; wires that end beside it: not_2_out, controlledsubmultiplex_9_p5, controlledsubmultiplex_9_p2, controlledsubmultiplex_11_p5, controlledsubmultiplex_12_p5, controlledsubmultiplex_12_p6
  // ControlledSubMultiplex controlledsubmultiplex_13: pin names not known; wires that end beside it: 1'b0, controlledsubmultiplex_13_p2, controlledsubmultiplex_13_p2, controlledsubmultiplex_12_p5, controlledsubmultiplex_13_p5
  not not_7 (Quotient[3], controlledsubmultiplex_13_p2);
  // ControlledSubMultiplex controlledsubmultiplex_14: pin names not known; wires that end beside it: 1'b0, controlledsubmultiplex_11_p6, controlledsubmultiplex_6_p2, x[11], controlledsubmultiplex_14_p5, controlledsubmultiplex_14_p6
  // ControlledSubMultiplex controlledsubmultiplex_15: pin names not known; wires that end beside it: controlledsubmultiplex_11_p1, controlledsubmultiplex_12_p6, controlledsubmultiplex_9_p2, controlledsubmultiplex_14_p5, controlledsubmultiplex_15_p5, controlledsubmultiplex_15_p6
  // ControlledSubMultiplex controlledsubmultiplex_16: pin names not known; wires that end beside it: not_2_out, controlledsubmultiplex_13_p5, controlledsubmultiplex_13_p2, controlledsubmultiplex_15_p5, controlledsubmultiplex_16_p5, controlledsubmultiplex_16_p6
  // ControlledSubMultiplex controlledsubmultiplex_17: pin names not known; wires that end beside it: 1'b0, controlledsubmultiplex_17_p2, controlledsubmultiplex_17_p2, controlledsubmultiplex_16_p5, controlledsubmultiplex_17_p5
  not not_8 (not_8_out, controlledsubmultiplex_6_p2);
  not not_9 (Quotient[2], controlledsubmultiplex_17_p2);
  // ControlledSubMultiplex controlledsubmultiplex_18: pin names not known; wires that end beside it: 1'b1, controlledsubmultiplex_14_p6, controlledsubmultiplex_6_p2, x[10], controlledsubmultiplex_18_p5, 1'b0
  // ControlledSubMultiplex controlledsubmultiplex_19: pin names not known; wires that end beside it: not_8_out, controlledsubmultiplex_15_p6, controlledsubmultiplex_9_p2, controlledsubmultiplex_18_p5, controlledsubmultiplex_19_p5, controlledsubmultiplex_19_p6
  // ControlledSubMultiplex controlledsubmultiplex_20: pin names not known; wires that end beside it: controlledsubmultiplex_11_p1, controlledsubmultiplex_16_p6, controlledsubmultiplex_13_p2, controlledsubmultiplex_19_p5, controlledsubmultiplex_20_p5, controlledsubmultiplex_20_p6
  // ControlledSubMultiplex controlledsubmultiplex_21: pin names not known; wires that end beside it: not_2_out, controlledsubmultiplex_17_p5, controlledsubmultiplex_17_p2, controlledsubmultiplex_20_p5, controlledsubmultiplex_21_p5, controlledsubmultiplex_21_p6
  // ControlledSubMultiplex controlledsubmultiplex_22: pin names not known; wires that end beside it: 1'b0, controlledsubmultiplex_22_p2, controlledsubmultiplex_22_p2, controlledsubmultiplex_21_p5, controlledsubmultiplex_22_p5
  not not_10 (Quotient[1], controlledsubmultiplex_22_p2);
  // ControlledSubMultiplex controlledsubmultiplex_23: pin names not known; wires that end beside it: 1'b0, controlledsubmultiplex_19_p6, controlledsubmultiplex_9_p2, x[9], controlledsubmultiplex_23_p5, controlledsubmultiplex_23_p6
  // ControlledSubMultiplex controlledsubmultiplex_24: pin names not known; wires that end beside it: not_8_out, controlledsubmultiplex_20_p6, controlledsubmultiplex_13_p2, controlledsubmultiplex_23_p5, controlledsubmultiplex_24_p5, controlledsubmultiplex_24_p6
  // ControlledSubMultiplex controlledsubmultiplex_25: pin names not known; wires that end beside it: controlledsubmultiplex_11_p1, controlledsubmultiplex_21_p6, controlledsubmultiplex_17_p2, controlledsubmultiplex_24_p5, controlledsubmultiplex_25_p5, controlledsubmultiplex_25_p6
  // ControlledSubMultiplex controlledsubmultiplex_26: pin names not known; wires that end beside it: not_2_out, controlledsubmultiplex_22_p5, controlledsubmultiplex_22_p2, controlledsubmultiplex_25_p5, controlledsubmultiplex_26_p5, controlledsubmultiplex_26_p6
  // ControlledSubMultiplex controlledsubmultiplex_27: pin names not known; wires that end beside it: 1'b0, controlledsubmultiplex_27_p2, controlledsubmultiplex_27_p2, controlledsubmultiplex_26_p5, controlledsubmultiplex_27_p5
  not not_11 (Quotient[0], controlledsubmultiplex_27_p2);
  // ControlledSubMultiplex controlledsubmultiplex_28: pin names not known; wires that end beside it: 1'b1, controlledsubmultiplex_23_p6, controlledsubmultiplex_9_p2, x[8], controlledsubmultiplex_28_p5, 1'b0
  // ControlledSubMultiplex controlledsubmultiplex_29: pin names not known; wires that end beside it: controlledsubmultiplex_29_p1, controlledsubmultiplex_24_p6, controlledsubmultiplex_13_p2, controlledsubmultiplex_28_p5, controlledsubmultiplex_29_p5, controlledsubmultiplex_29_p6
  not not_12 (controlledsubmultiplex_29_p1, controlledsubmultiplex_9_p2);
  // ControlledSubMultiplex controlledsubmultiplex_30: pin names not known; wires that end beside it: not_8_out, controlledsubmultiplex_25_p6, controlledsubmultiplex_17_p2, controlledsubmultiplex_29_p5, controlledsubmultiplex_30_p5, controlledsubmultiplex_30_p6
  // ControlledSubMultiplex controlledsubmultiplex_31: pin names not known; wires that end beside it: controlledsubmultiplex_11_p1, controlledsubmultiplex_26_p6, controlledsubmultiplex_22_p2, controlledsubmultiplex_30_p5, controlledsubmultiplex_31_p5, controlledsubmultiplex_31_p6
  // ControlledSubMultiplex controlledsubmultiplex_32: pin names not known; wires that end beside it: not_2_out, controlledsubmultiplex_27_p5, controlledsubmultiplex_27_p2, controlledsubmultiplex_31_p5, controlledsubmultiplex_32_p5
  // ControlledSubMultiplex controlledsubmultiplex_33: pin names not known; wires that end beside it: 1'b0, controlledsubmultiplex_29_p6, controlledsubmultiplex_13_p2, x[7], controlledsubmultiplex_33_p5, controlledsubmultiplex_33_p6
  // ControlledSubMultiplex controlledsubmultiplex_34: pin names not known; wires that end beside it: controlledsubmultiplex_29_p1, controlledsubmultiplex_30_p6, controlledsubmultiplex_17_p2, controlledsubmultiplex_33_p5, controlledsubmultiplex_34_p5, controlledsubmultiplex_34_p6
  // ControlledSubMultiplex controlledsubmultiplex_35: pin names not known; wires that end beside it: not_8_out, controlledsubmultiplex_31_p6, controlledsubmultiplex_22_p2, controlledsubmultiplex_34_p5, controlledsubmultiplex_35_p5, controlledsubmultiplex_35_p6
  // ControlledSubMultiplex controlledsubmultiplex_36: pin names not known; wires that end beside it: controlledsubmultiplex_11_p1, controlledsubmultiplex_32_p5, controlledsubmultiplex_27_p2, controlledsubmultiplex_35_p5, controlledsubmultiplex_36_p5
  not not_13 (not_13_out, controlledsubmultiplex_13_p2);
  // ControlledSubMultiplex controlledsubmultiplex_37: pin names not known; wires that end beside it: 1'b1, controlledsubmultiplex_33_p6, controlledsubmultiplex_13_p2, x[6], controlledsubmultiplex_37_p5, 1'b0
  // ControlledSubMultiplex controlledsubmultiplex_38: pin names not known; wires that end beside it: not_13_out, controlledsubmultiplex_34_p6, controlledsubmultiplex_17_p2, controlledsubmultiplex_37_p5, controlledsubmultiplex_38_p5, controlledsubmultiplex_38_p6
  // ControlledSubMultiplex controlledsubmultiplex_39: pin names not known; wires that end beside it: controlledsubmultiplex_29_p1, controlledsubmultiplex_35_p6, controlledsubmultiplex_22_p2, controlledsubmultiplex_38_p5, controlledsubmultiplex_39_p5, controlledsubmultiplex_39_p6
  // ControlledSubMultiplex controlledsubmultiplex_40: pin names not known; wires that end beside it: not_8_out, controlledsubmultiplex_36_p5, controlledsubmultiplex_27_p2, controlledsubmultiplex_39_p5, controlledsubmultiplex_40_p5
  // ControlledSubMultiplex controlledsubmultiplex_41: pin names not known; wires that end beside it: 1'b0, controlledsubmultiplex_38_p6, controlledsubmultiplex_17_p2, x[5], controlledsubmultiplex_41_p5, controlledsubmultiplex_41_p6
  // ControlledSubMultiplex controlledsubmultiplex_42: pin names not known; wires that end beside it: not_13_out, controlledsubmultiplex_39_p6, controlledsubmultiplex_22_p2, controlledsubmultiplex_41_p5, controlledsubmultiplex_42_p5, controlledsubmultiplex_42_p6
  // ControlledSubMultiplex controlledsubmultiplex_43: pin names not known; wires that end beside it: controlledsubmultiplex_29_p1, controlledsubmultiplex_40_p5, controlledsubmultiplex_27_p2, controlledsubmultiplex_42_p5, controlledsubmultiplex_43_p5
  // ControlledSubMultiplex controlledsubmultiplex_44: pin names not known; wires that end beside it: 1'b1, controlledsubmultiplex_41_p6, controlledsubmultiplex_17_p2, x[4], controlledsubmultiplex_44_p5, 1'b0
  // ControlledSubMultiplex controlledsubmultiplex_45: pin names not known; wires that end beside it: controlledsubmultiplex_45_p1, controlledsubmultiplex_42_p6, controlledsubmultiplex_22_p2, controlledsubmultiplex_44_p5, controlledsubmultiplex_45_p5, controlledsubmultiplex_45_p6
  not not_14 (controlledsubmultiplex_45_p1, controlledsubmultiplex_17_p2);
  // ControlledSubMultiplex controlledsubmultiplex_46: pin names not known; wires that end beside it: not_13_out, controlledsubmultiplex_43_p5, controlledsubmultiplex_27_p2, controlledsubmultiplex_45_p5, controlledsubmultiplex_46_p5
  // ControlledSubMultiplex controlledsubmultiplex_47: pin names not known; wires that end beside it: 1'b0, controlledsubmultiplex_45_p6, controlledsubmultiplex_22_p2, x[3], controlledsubmultiplex_47_p5, controlledsubmultiplex_47_p6
  // ControlledSubMultiplex controlledsubmultiplex_48: pin names not known; wires that end beside it: controlledsubmultiplex_45_p1, controlledsubmultiplex_46_p5, controlledsubmultiplex_27_p2, controlledsubmultiplex_47_p5, controlledsubmultiplex_48_p5
  not not_15 (not_15_out, controlledsubmultiplex_22_p2);
  // ControlledSubMultiplex controlledsubmultiplex_49: pin names not known; wires that end beside it: 1'b1, controlledsubmultiplex_47_p6, controlledsubmultiplex_22_p2, x[2], controlledsubmultiplex_49_p5, 1'b0
  // ControlledSubMultiplex controlledsubmultiplex_50: pin names not known; wires that end beside it: not_15_out, controlledsubmultiplex_48_p5, controlledsubmultiplex_27_p2, controlledsubmultiplex_49_p5, controlledsubmultiplex_50_p5
  // ControlledSubMultiplex controlledsubmultiplex_51: pin names not known; wires that end beside it: 1'b0, controlledsubmultiplex_50_p5, controlledsubmultiplex_27_p2, x[1], controlledsubmultiplex_51_p5
  // ControlledSubMultiplex controlledsubmultiplex_52: pin names not known; wires that end beside it: 1'b1, controlledsubmultiplex_51_p5, controlledsubmultiplex_27_p2, x[0], 1'b0

  assign Quotient[15:8] = {8{1'b0}};
endmodule
