// Digital circuit CPU.dig as structural Verilog
module CPU (
  input  clk,
  input  reset,
  input  [15:0] DEV_IN_0,
  input  DEV_SUBMIT,
  input  [15:0] DEV_IN_1,
  input  [15:0] DEV_IN_2,
  input  [15:0] DEV_IN_3,
  input  manual_clock,
  output DEV_RELEASE,
  output [15:0] DEV_OUT_0,
  output [15:0] DEV_OUT_1,
  output [15:0] DEV_OUT_2,
  output [15:0] DEV_OUT_3,
  output DEV_AWAIT,
  output [15:0] DEV_OUT_4,
  output [15:0] DEV_OUT_5,
  output [15:0] DEV_OUT_6,
  output [15:0] DEV_OUT_7,
  output [15:0] DEV_OUT_8,
  output [15:0] DEV_OUT_9,
  output [15:0] DEV_OUT_10,
  output [15:0] DEV_OUT_11,
  output [1:0] DEV_SELECT
);

  wire inputdecoder_1_p1, inputdecoder_1_p3, inputdecoder_1_p6, inputdecoder_2_p6, jmpdecoder_1_p2,
       jmpdecoder_1_p3, jmpdecoder_1_p4, K_out, memoryperf_1_p4, not_1_out, or_1_out, pc_1_p2, register_1_p3;
  wire [3:0] multiplexer_1_out;
  wire [7:0] alu_1_p6;
  wire [14:4] multiplexer_1_out_2;
  wire [15:0] memoryperf_1_p2, multiplexer_2_out, multiplexer_3_out, pc_1_p4, register_1_p1, ROM_d;

  // Probe IP on pc_1_p4
  ROM #(.AddrBits(16), .isProgramMemory("true"), .Bits(16)) ROM (.A(pc_1_p4), .sel(1'b1), .D(ROM_d));
  // Probe inst on ROM_d
  not not_1 (not_1_out, ROM_d[15]);
  or or_1 (or_1_out, multiplexer_1_out_2[8], not_1_out);
  Multiplexer #(.Bits(15)) multiplexer_1 (
    .sel(ROM_d[15]), .in_0({15{1'b0}}), .in_1(ROM_d[14:0]), .out({multiplexer_1_out_2, multiplexer_1_out}));
  // Probe C inst flag on ROM_d[15]
  // Probe ALU_out on register_1_p1
  Multiplexer #(.Bits(16)) multiplexer_2 (
    .sel(not_1_out), .in_0(register_1_p1), .in_1({1'b0, ROM_d[14:0]}), .out(multiplexer_2_out));
  // Probe dest on multiplexer_1_out_2[9:7]
  // Register register_1: pin names not known; wires that end beside it: register_1_p1, multiplexer_1_out_2[9], register_1_p3
  // Register register_2: pin names not known; wires that end beside it: multiplexer_2_out, or_1_out, register_1_p3
  // MemoryPerf memoryperf_1: pin names not known; wires that end beside it: register_1_p1, memoryperf_1_p2[14:0], multiplexer_1_out_2[14], memoryperf_1_p4, multiplexer_1_out_2[7]
  // Probe memory bit on multiplexer_1_out_2[14]
  // Probe D on inputdecoder_1_p1
  // Probe A on memoryperf_1_p2
  // Probe M on inputdecoder_1_p3
  // InputDecoder inputdecoder_1: pin names not known; wires that end beside it: inputdecoder_1_p1, memoryperf_1_p2, inputdecoder_1_p3, multiplexer_1_out_2[14], multiplexer_1_out_2[13:12], inputdecoder_1_p6
  // InputDecoder inputdecoder_2: pin names not known; wires that end beside it: inputdecoder_1_p1, memoryperf_1_p2, inputdecoder_1_p3, multiplexer_1_out_2[14], multiplexer_1_out_2[11:10], inputdecoder_2_p6
  // Probe x on inputdecoder_1_p6
  // Probe y on inputdecoder_2_p6
  and and_1 (register_1_p3, pc_1_p2, memoryperf_1_p4);
  // ALUDecoder aludecoder_1: pin names not known; wires that end beside it: multiplexer_1_out
  // Probe command on multiplexer_1_out
  // JMPDecoder jmpdecoder_1: pin names not known; wires that end beside it: multiplexer_1_out_2[6:4], jmpdecoder_1_p2, jmpdecoder_1_p3, jmpdecoder_1_p4
  // Probe jmp on multiplexer_1_out_2[6:4]
  // PC pc_1: pin names not known; wires that end beside it: memoryperf_1_p2, pc_1_p2, memoryperf_1_p4, pc_1_p4, reset, jmpdecoder_1_p3
  Multiplexer #(.Selector_Bits(2), .Bits(16)) multiplexer_3 (
    .sel(DEV_SELECT), .in_0(DEV_IN_0), .in_1(DEV_IN_1), .in_2(DEV_IN_2), .in_3(DEV_IN_3),
    .out(multiplexer_3_out));
  Button K (.out(K_out));
  Multiplexer multiplexer_4 (.sel(manual_clock), .in_0(clk), .in_1(K_out), .out(memoryperf_1_p4));
  // Probe zy on alu_1_p6[5]
  // ALU alu_1: pin names not known; wires that end beside it: inputdecoder_1_p6, inputdecoder_2_p6, register_1_p1, jmpdecoder_1_p2, jmpdecoder_1_p4, alu_1_p6, alu_1_p6[7], alu_1_p6[6], alu_1_p6[5], alu_1_p6[4], alu_1_p6[3:1], alu_1_p6[0]
  // Probe f on alu_1_p6[3:1]
  // Probe zx on alu_1_p6[7]
  // Probe no on alu_1_p6[0]
  // Probe ny on alu_1_p6[4]
  // Probe nx on alu_1_p6[6]

  // Notes on the sheet:
  //   clk: Hz: 30
  //   D
  //   A
endmodule
