// Digital circuit ALU.dig as structural Verilog
module ALU (
  input  zx,
  input  nx,
  input  zy,
  input  ny,
  input  [2:0] f,
  input  no,
  input  [15:0] x,
  input  [15:0] y,
  output [15:0] out,
  output ng,
  output zr
);

  wire or_1_out, or_2_out;
  wire [15:0] add16_1_p3, and_1_out, div16_1_p3, div16_1_p4, mul16_1_p3, multiplexer_1_out,
       multiplexer_2_out, multiplexer_3_out, multiplexer_4_out, multiplexer_6_out, not_1_out, not_2_out,
       not_3_out, sqrt16_1_p2, undriven, xor_1_out;

  Multiplexer #(.Bits(16)) multiplexer_1 (.sel(zx), .in_0(x), .in_1({16{1'b0}}), .out(multiplexer_1_out));
  Multiplexer #(.Bits(16)) multiplexer_2 (.sel(zy), .in_0(y), .in_1({16{1'b0}}), .out(multiplexer_2_out));
  assign not_1_out = ~multiplexer_2_out;  // Not not_1, 16 bits wide
  Multiplexer #(.Bits(16)) multiplexer_3 (
    .sel(ny), .in_0(multiplexer_2_out), .in_1(not_1_out), .out(multiplexer_3_out));
  assign not_2_out = ~multiplexer_1_out;  // Not not_2, 16 bits wide
  Multiplexer #(.Bits(16)) multiplexer_4 (
    .sel(nx), .in_0(multiplexer_1_out), .in_1(not_2_out), .out(multiplexer_4_out));
  Multiplexer #(.Bits(16)) multiplexer_5 (.sel(no), .in_0(multiplexer_6_out), .in_1(not_3_out), .out({ng, out[14:0]}));
  assign not_3_out = ~multiplexer_6_out;  // Not not_3, 16 bits wide
  nor nor_1 (zr, or_2_out, or_1_out);
  Multiplexer #(.Selector_Bits(3), .Bits(16)) multiplexer_6 (
    .sel(f), .in_0(and_1_out), .in_1(add16_1_p3), .in_2(mul16_1_p3), .in_3(div16_1_p3), .in_4(div16_1_p4),
    .in_5(undriven), .in_6(sqrt16_1_p2), .in_7(xor_1_out), .out(multiplexer_6_out));
  or or_1 (or_1_out, out[8], out[9], out[10], out[11], out[12], out[13], out[14], ng);
  or or_2 (or_2_out, out[0], out[1], out[2], out[3], out[4], out[5], out[6], out[7]);
  // Sqrt16 sqrt16_1: pin names not known; wires that end beside it: multiplexer_4_out, sqrt16_1_p2
  // Div16 div16_1: pin names not known; wires that end beside it: multiplexer_4_out, multiplexer_3_out, div16_1_p3, div16_1_p4
  assign and_1_out = multiplexer_4_out & multiplexer_3_out;  // And and_1, 16 bits wide
  assign xor_1_out = multiplexer_4_out ^ multiplexer_3_out;  // XOr xor_1, 16 bits wide
  // Add16 add16_1: pin names not known; wires that end beside it: multiplexer_4_out, multiplexer_3_out, add16_1_p3
  // Abs16 abs16_1: pin names not known; wires that end beside it: multiplexer_4_out
  // Mul16 mul16_1: pin names not known; wires that end beside it: multiplexer_4_out, multiplexer_3_out, mul16_1_p3

  assign out[15] = ng;
endmodule

/* Test case Test flags:
x                  y                  out                zx nx zy ny f      no zr ng
0b0000000000000000 0b0000000000000000 0b0000000000000000 0  0  0  0  0b000  0  1  0
0b0000000000000000 0b0000000000000000 0b1111111111111111 0  0  0  0  0b000  1  0  1
0b0000000000000001 0b0000000000000001 0b0000000000000000 1  0  0  0  0b000  0  1  0
0b0000000000000001 0b0000000000000001 0b0000000000000000 0  0  1  0  0b000  0  1  0
0b0000000000000001 0b0000000000000001 0b1111111111111110 0  1  0  1  0b000  0  0  1
0b1111111111111110 0b1111111111111110 0b0000000000000001 0  0  0  0  0b000  1  0  0
*/

/* Test case AND:
x                  y                  out                zx nx zy ny f      no zr ng
0b0000000000000000 0b0000000000000000 0b0000000000000000 0  0  0  0  0b000  0  1  0
0b1111111111111111 0b1111111111111111 0b1111111111111111 0  0  0  0  0b000  0  0  1
0b1111111111111111 0b0000000000000000 0b0000000000000000 0  0  0  0  0b000  0  1  0
0b1010101010101010 0b0101010101010101 0b0000000000000000 0  0  0  0  0b000  0  1  0
0b1010101010101010 0b0101010101010101 0b1010101010101010 0  0  0  1  0b000  0  0  1
*/

/* Test case OR:
x                  y                  out                zx nx zy ny f      no zr ng
0b0000000000000000 0b0000000000000000 0b0000000000000000 0  1  0  1  0b000  1  1  0
0b1111111111111111 0b0000000000000000 0b1111111111111111 0  1  0  1  0b000  1  0  1
0b1010101010101010 0b0101010101010101 0b1111111111111111 0  1  0  1  0b000  1  0  1
0b1010101010101010 0b0000000000000000 0b1010101010101010 0  1  0  1  0b000  1  0  1
0b1010101010101010 0b0000000000000000 0b0101010101010101 0  1  0  1  0b000  0  0  0
0b1010101010101010 0b0101010101010101 0b1111111111111111 0  1  0  1  0b000  1  0  1
*/

/* Test case NOT:
x                  y                  out                zx nx zy ny f      no zr ng
0b1010101010101010 0b0000000000000000 0b0101010101010101 0  1  1  1  0b000  0  0  0
0b1010101010101010 0b0000000000000000 0b1010101010101010 0  1  1  1  0b000  1  0  1
*/

/* Test case ADD:
x                  y                  out                zx nx zy ny f      no zr ng
0b0000000000000001 0b0000000000000001 0b0000000000000001 1  0  0  0  0b001  0  0  0
0b0000000000000001 0b0000000000000001 0b0000000000000001 0  0  1  0  0b001  0  0  0
0b0000000000000001 0b0000000000000001 0b0000000000000010 0  0  0  0  0b001  0  0  0
0b0000000000000001 0b1111111111111111 0b0000000000000000 0  0  0  0  0b001  0  1  0
0b1111111111111111 0b1111111111111111 0b1111111111111110 0  0  0  0  0b001  0  0  1
0b1111111111111111 0b0000000000000001 0b0000000000000000 0  0  0  0  0b001  0  1  0
0b0111111111111111 0b0000000000000001 0b1000000000000000 0  0  0  0  0b001  0  0  1
0b0000000000000001 0b0000000000000001 0b1111111111111111 0  1  0  0  0b001  0  0  1
*/

/* Test case SUB:
x                  y                  out                zx nx zy ny f      no zr ng
0b0000000000000001 0b0000000000000001 0b1111111111111111 1  1  0  0  0b001  1  0  1
0b0000000000000001 0b0000000000000001 0b0000000000000001 0  1  1  0  0b001  1  0  0
0b0000000000000001 0b0000000000000001 0b0000000000000000 0  1  0  0  0b001  1  1  0
0b0000000000000001 0b1111111111111111 0b0000000000000010 0  1  0  0  0b001  1  0  0
0b1111111111111111 0b1111111111111111 0b0000000000000000 0  1  0  0  0b001  1  1  0
*/

/* Test case NEG:
x                  y                  out                zx nx zy ny f      no zr ng
0b0000000000000001 0b0000000000000000 0b1111111111111111 0  0  1  1  0b001  1  0  1
0b0111111111111111 0b0000000000000000 0b1000000000000001 0  0  1  1  0b001  1  0  1
0b0111111111111111 0b0000000000000000 0b1000000000000001 0  0  1  1  0b001  1  0  1
*/

/* Test case MULT:
x                  y                  out                zx nx zy ny f      no zr ng
0b0000000000000001 0b0000000000000000 0b0000000000000000 0  0  0  0  0b010  0  1  0
0b0000000000000001 0b0000000000000001 0b0000000000000000 1  0  0  0  0b010  0  1  0
0b0000000000000001 0b1111111111111111 0b1111111111111111 0  0  0  0  0b010  0  0  1
0b0000000000000001 0b0000000000000000 0b0000000000000000 0  0  0  0  0b010  0  1  0
0b1111111111111111 0b0000000000000001 0b1111111111111111 0  0  0  0  0b010  0  0  1
0b1111111111111111 0b1111111111111111 0b0000000000000001 0  0  0  0  0b010  0  0  0
0b0111111111111111 0b0000000000000010 0b1111111111111110 0  0  0  0  0b010  0  0  1
*/

/* Test case DIV:
x                  y                  out                zx nx zy ny f      no zr ng
0b0000000000000001 0b0000000000000001 0b0000000000000001 0  0  0  0  0b011  0  0  0
0b0000000000000001 0b0000000000000001 0b0000000000000000 1  0  0  0  0b011  0  1  0
0b0000000000000001 0b1111111111111111 0b1111111111111111 0  0  0  0  0b011  0  0  1
0b0000000000000000 0b1111111111111111 0b0000000000000000 0  0  0  0  0b011  0  1  0
0b1111111111111111 0b0000000000000001 0b1111111111111111 0  0  0  0  0b011  0  0  1
0b1111111111111111 0b1111111111111111 0b0000000000000001 0  0  0  0  0b011  0  0  0
0b0111111111111111 0b0000000000000010 0b0011111111111111 0  0  0  0  0b011  0  0  0
0b0000000000000001 0b0000000000000100 0b0000000000000000 0  0  0  0  0b011  0  1  0
0b0000000000000101 0b0000000000000100 0b0000000000000001 0  0  0  0  0b011  0  0  0
0b1111111111111111 0b0000000000000100 0b1111111111111111 0  0  0  0  0b011  0  0  1
0b1111111111111011 0b0000000000000100 0b1111111111111110 0  0  0  0  0b011  0  0  1
0b0000000000000001 0b1111111111111100 0b1111111111111111 0  0  0  0  0b011  0  0  1
0b0000000000000101 0b1111111111111100 0b1111111111111110 0  0  0  0  0b011  0  0  1
0b1111111111111111 0b1111111111111100 0b0000000000000000 0  0  0  0  0b011  0  1  0
0b1111111111111011 0b1111111111111100 0b0000000000000001 0  0  0  0  0b011  0  0  0
0b0000000000000001 0b0000000000000000 0b1111111111111111 0  0  0  0  0b011  0  0  1
0b1111111111111111 0b0000000000000000 0b0000000000000000 0  0  0  0  0b011  0  1  0
*/

/* Test case MOD:
x                  y                  out                zx nx zy ny f      no zr ng
0b0000000000000001 0b0000000000000100 0b0000000000000001 0  0  0  0  0b100  0  0  0
0b0000000000000101 0b0000000000000100 0b0000000000000001 0  0  0  0  0b100  0  0  0
0b1111111111111111 0b0000000000000100 0b0000000000000011 0  0  0  0  0b100  0  0  0
0b1111111111111011 0b0000000000000100 0b0000000000000011 0  0  0  0  0b100  0  0  0
0b0000000000000001 0b1111111111111100 0b1111111111111101 0  0  0  0  0b100  0  0  1
0b0000000000000101 0b1111111111111100 0b1111111111111101 0  0  0  0  0b100  0  0  1
0b1111111111111111 0b1111111111111100 0b1111111111111111 0  0  0  0  0b100  0  0  1
0b1111111111111011 0b1111111111111100 0b1111111111111111 0  0  0  0  0b100  0  0  1
0b0000000000000001 0b0000000000000000 0b0000000000000001 0  0  0  0  0b100  0  0  0
0b1111111111111111 0b0000000000000000 0b1111111111111111 0  0  0  0  0b100  0  0  1
*/

/* Test case ABS:
x                  y                  out                zx nx zy ny f      no zr ng
0b0000000000000001 0b0000000000000000 0b0000000000000001 0  0  0  0  0b101  0  0  0
0b1111111111111111 0b0000000000000000 0b0000000000000001 0  0  0  0  0b101  0  0  0
0b1000000000000001 0b0000000000000000 0b0111111111111111 0  0  0  0  0b101  0  0  0
*/

/* Test case SQRT:
x                  y                  out                zx nx zy ny f      no zr ng
0b0000000000000000 0b0000000000000000 0b0000000000000000 0  0  0  0  0b110  0  1  0
0b0000000000000001 0b0000000000000000 0b0000000000000001 0  0  0  0  0b110  0  0  0
0b0000000000000010 0b0000000000000000 0b0000000000000001 0  0  0  0  0b110  0  0  0
0b0000000000000100 0b0000000000000000 0b0000000000000010 0  0  0  0  0b110  0  0  0
0b0111111111111111 0b0000000000000000 0b0000000010110101 0  0  0  0  0b110  0  0  0
0b1111111111111111 0b0000000000000000 0b0000000011111111 0  0  0  0  0b110  0  0  0
0b1000000000000000 0b0000000000000000 0b0000000010110101 0  0  0  0  0b110  0  0  0
*/

/* Test case NOP:
x                  y                  out                zx nx zy ny f      no zr ng
0b0000000000000000 0b0000000000000000 0b0000000000000000 0  0  1  1  0b000  0  1  0
0b0000000000000001 0b0000000000000000 0b0000000000000001 0  0  1  1  0b000  0  0  0
*/

/* Test case XOR:
x                  y                  out                zx nx zy ny f      no zr ng
0b0000000000000000 0b0000000000000000 0b0000000000000000 0  0  0  0  0b111  0  1  0
0b1111111111111111 0b0000000000000000 0b1111111111111111 0  0  0  0  0b111  0  0  1
0b0000000000000000 0b1111111111111111 0b1111111111111111 0  0  0  0  0b111  0  0  1
0b1010101010101010 0b0101010101010101 0b1111111111111111 0  0  0  0  0b111  0  0  1
0b1111111111111111 0b1111111111111111 0b0000000000000000 0  0  0  0  0b111  0  1  0
*/
