// Digital circuit ControlledSubMultiplex.dig as structural Verilog
module ControlledSubMultiplex (
  input  os,
  input  y,
  input  x,
  input  L,
  output Loan,
  output Difference
);

  wire and_1_out, and_2_out, not_1_out, undriven;

  FullSubtractor fullsubtractor_1 (.A(x), .B(y), .L(L));  // open: Difference, Loan
  and and_1 (and_1_out, x, os);
  or or_1 (Difference, and_2_out, and_1_out);
  not not_1 (not_1_out, os);
  and and_2 (and_2_out, not_1_out, undriven);
endmodule
