// Digital circuit FullSubtractor.dig as structural Verilog
module FullSubtractor (
  input  A,
  input  B,
  input  L,
  output Difference,
  output Loan
);

  wire and_1_out, and_2_out, not_1_out, xnor_1_out, xor_1_out;

  xor xor_1 (xor_1_out, A, B);
  xnor xnor_1 (xnor_1_out, A, B);
  not not_1 (not_1_out, A);
  and and_1 (and_1_out, not_1_out, B);
  xor xor_2 (Difference, xor_1_out, L);
  and and_2 (and_2_out, L, xnor_1_out);
  or or_1 (Loan, and_2_out, and_1_out);
endmodule
