// Digital circuit Inc16.dig as structural Verilog
module Inc16 (
  input  [15:0] in,
  output [15:0] out
);

  wire and_1_out, and_2_out, and_3_out, and_4_out, and_5_out, and_6_out, and_7_out, and_8_out, and_9_out,
       and_10_out, and_11_out, and_12_out, and_13_out, and_14_out, and_15_out;

  xor xor_1 (out[12], in[12], and_7_out);
  and and_1 (and_1_out, and_7_out, in[12]);
  xor xor_2 (out[13], in[13], and_1_out);
  and and_2 (and_2_out, and_1_out, in[13]);
  xor xor_3 (out[14], in[14], and_2_out);
  and and_3 (and_3_out, and_2_out, in[14]);
  xor xor_4 (out[15], in[15], and_3_out);
  xor xor_5 (out[8], in[8], and_11_out);
  and and_4 (and_4_out, and_11_out, in[8]);
  xor xor_6 (out[9], in[9], and_4_out);
  and and_5 (and_5_out, and_4_out, in[9]);
  xor xor_7 (out[10], in[10], and_5_out);
  and and_6 (and_6_out, and_5_out, in[10]);
  xor xor_8 (out[11], in[11], and_6_out);
  and and_7 (and_7_out, and_6_out, in[11]);
  xor xor_9 (out[4], in[4], and_15_out);
  and and_8 (and_8_out, and_15_out, in[4]);
  xor xor_10 (out[5], in[5], and_8_out);
  and and_9 (and_9_out, and_8_out, in[5]);
  xor xor_11 (out[6], in[6], and_9_out);
  and and_10 (and_10_out, and_9_out, in[6]);
  xor xor_12 (out[7], in[7], and_10_out);
  and and_11 (and_11_out, and_10_out, in[7]);
  xor xor_13 (out[0], in[0], 1'b1);
  and and_12 (and_12_out, 1'b1, in[0]);
  xor xor_14 (out[1], in[1], and_12_out);
  and and_13 (and_13_out, and_12_out, in[1]);
  xor xor_15 (out[2], in[2], and_13_out);
  and and_14 (and_14_out, and_13_out, in[2]);
  xor xor_16 (out[3], in[3], and_14_out);
  and and_15 (and_15_out, and_14_out, in[3]);
endmodule
