// Digital circuit Neg16.dig as structural Verilog
module Neg16 (
  input  [15:0] in,
  output [15:0] out
);

  wire [15:0] not_1_out;

  assign not_1_out = ~in;  // Not not_1, 16 bits wide
  // Inc16 inc16_1: pin names not known; wires that end beside it: not_1_out
endmodule
