// Digital circuit InstDecoder.dig as structural Verilog
module InstDecoder (
  input  [15:0] inst,
  output [3:0] operation,
  output [2:0] jmp_cond,
  output [1:0] y_sel,
  output [1:0] x_sel,
  output memory_bit,
  output C_inst_flag,
  output M_load,
  output A_load,
  output D_load
);

  Multiplexer #(.Bits(15)) multiplexer_1 (
    .sel(inst[15]), .in_0({15{1'b0}}), .in_1(inst[14:0]),
    .out({memory_bit, x_sel, y_sel, D_load, A_load, M_load, jmp_cond, operation}));
  // Pins of 3 and 4 bits meet at operation

  assign C_inst_flag = inst[15];
endmodule
