// Digital circuit JMPDecoder.dig as structural Verilog
module JMPDecoder (
  input  zr,
  input  ng,
  input  [2:0] jmp,
  output out
);

  wire demultiplexer_1_out_0, demultiplexer_1_out_1, not_1_out, not_2_out, or_1_out;

  not not_1 (not_1_out, zr);
  or or_1 (or_1_out, zr, ng);
  Demultiplexer demultiplexer_1 (
    .sel(ng), .in(not_1_out), .out_0(demultiplexer_1_out_0), .out_1(demultiplexer_1_out_1));
  not not_2 (not_2_out, ng);
  Multiplexer #(.Selector_Bits(3)) multiplexer_1 (
    .sel(jmp), .in_0(1'b0), .in_1(demultiplexer_1_out_0), .in_2(zr), .in_3(not_2_out),
    .in_4(demultiplexer_1_out_1), .in_5(not_1_out), .in_6(or_1_out), .in_7(1'b1), .out(out));
endmodule
