// Digital circuit MemoryPerf.dig as structural Verilog
module MemoryPerf (
  input  [15:0] in,
  input  load,
  input  [14:0] address,
  input  clk,
  input  [15:0] device_in,
  input  device_submit,
  input  memory_bit,
  output device_release,
  output [15:0] out,
  output intok,
  output [63:0] device_out_0_3,
  output [63:0] device_out_4_7,
  output [63:0] device_out_8_11,
  output device_await,
  output [1:0] device_select
);

  wire and_1_out, and_2_out, demultiplexer_1_out_0, demultiplexer_1_out_1, demultiplexer_2_out_0,
       demultiplexer_3_out_0, demultiplexer_4_out_0, demultiplexer_5_out_0, demultiplexer_6_out_1,
       demultiplexer_6_out_2, demultiplexer_6_out_3, not_1_out, not_2_out, not_3_out, or_1_out,
       ram4transparent_1_p1, undriven;
  wire [15:0] multiplexer_3_out, multiplexer_4_out, multiplexer_5_out, multiplexer_6_out, multiplexer_7_out,
       ramdualport_1_d, undriven_2, undriven_3, undriven_4;

  Demultiplexer demultiplexer_1 (
    .sel(address[14]), .in(load), .out_0(demultiplexer_1_out_0), .out_1(demultiplexer_1_out_1));
  Interruptor interruptor_1 (.address(address));  // open: interrupt
  RAMDualPort #(.AddrBits(14), .Bits(16)) ramdualport_1 (
    .A(address[13:0]), .Din(in), .str(demultiplexer_1_out_0), .C(clk), .ld(1'b1), .D(ramdualport_1_d));
  Demultiplexer #(.Selector_Bits(2)) demultiplexer_2 (
    .sel(address[13:12]), .in(demultiplexer_1_out_1), .out_0(demultiplexer_2_out_0));  // open: out_1, out_2, out_3
  Demultiplexer #(.Selector_Bits(3)) demultiplexer_3 (
    .sel(address[11:9]), .in(demultiplexer_2_out_0), .out_0(demultiplexer_3_out_0));  // open: out_1, out_2, out_3, out_4, out_5, out_6, out_7
  Demultiplexer #(.Selector_Bits(3)) demultiplexer_4 (
    .sel(address[8:6]), .in(demultiplexer_3_out_0), .out_0(demultiplexer_4_out_0));  // open: out_1, out_2, out_3, out_4, out_5, out_6, out_7
  Demultiplexer #(.Selector_Bits(2)) demultiplexer_5 (
    .sel(address[5:4]), .in(demultiplexer_4_out_0), .out_0(demultiplexer_5_out_0));  // open: out_1, out_2, out_3
  Demultiplexer #(.Selector_Bits(2)) demultiplexer_6 (
    .sel(address[3:2]), .in(demultiplexer_5_out_0), .out_1(demultiplexer_6_out_1),
    .out_2(demultiplexer_6_out_2), .out_3(demultiplexer_6_out_3));  // open: out_0
  // RAM4Transparent ram4transparent_1: pin names not known; wires that end beside it: ram4transparent_1_p1, in, demultiplexer_6_out_1, address[1:0], clk, device_release
  // RAM4Transparent ram4transparent_2: pin names not known; wires that end beside it: in, demultiplexer_6_out_2, address[1:0], clk
  // RAM4Transparent ram4transparent_3: pin names not known; wires that end beside it: in, demultiplexer_6_out_3, address[1:0], clk
  and and_1 (and_1_out, device_submit, device_await);
  not not_1 (not_1_out, memory_bit);
  not not_2 (not_2_out, ram4transparent_1_p1);
  Multiplexer #(.Bits(2)) multiplexer_1 (.sel(device_await), .in_0(2'b00), .in_1(address[1:0]), .out(device_select));
  DFF dff_1 (.in(and_1_out), .clk(clk));  // open: out
  or or_1 (or_1_out, not_1_out, not_2_out);
  DFF dff_2 (.in(device_release), .clk(clk));  // open: out
  or or_2 (intok, or_1_out, and_2_out);
  and and_2 (and_2_out, undriven, not_3_out);
  not not_3 (not_3_out, device_release);
  Multiplexer #(.Bits(16)) multiplexer_2 (
    .sel(address[14]), .in_0(ramdualport_1_d), .in_1(multiplexer_7_out), .out(out));
  not not_4 (device_await, intok);
  Multiplexer #(.Selector_Bits(2), .Bits(16)) multiplexer_3 (
    .sel(address[3:2]), .in_0(device_in), .in_1(undriven_2), .in_2(undriven_3), .in_3(undriven_4),
    .out(multiplexer_3_out));
  Multiplexer #(.Selector_Bits(2), .Bits(16)) multiplexer_4 (
    .sel(address[5:4]), .in_0(multiplexer_3_out), .in_1({16{1'b0}}), .in_2({16{1'b0}}), .in_3({16{1'b0}}),
    .out(multiplexer_4_out));
  Multiplexer #(.Selector_Bits(3), .Bits(16)) multiplexer_5 (
    .sel(address[8:6]), .in_0(multiplexer_4_out), .in_1({16{1'b0}}), .in_2({16{1'b0}}), .in_3({16{1'b0}}),
    .in_4({16{1'b0}}), .in_5({16{1'b0}}), .in_6({16{1'b0}}), .in_7({16{1'b0}}), .out(multiplexer_5_out));
  Multiplexer #(.Selector_Bits(3), .Bits(16)) multiplexer_6 (
    .sel(address[11:9]), .in_0(multiplexer_5_out), .in_1({16{1'b0}}), .in_2({16{1'b0}}), .in_3({16{1'b0}}),
    .in_4({16{1'b0}}), .in_5({16{1'b0}}), .in_6({16{1'b0}}), .in_7({16{1'b0}}), .out(multiplexer_6_out));
  Multiplexer #(.Selector_Bits(2), .Bits(16)) multiplexer_7 (
    .sel(address[13:12]), .in_0(multiplexer_6_out), .in_1({16{1'b0}}), .in_2({16{1'b0}}), .in_3({16{1'b0}}),
    .out(multiplexer_7_out));
endmodule
