// Digital circuit PC.dig as structural Verilog
module PC (
  input  clk,
  input  [15:0] in,
  input  load,
  input  reset,
  input  inc,
  output [15:0] out
);

  wire delay_1_out, or_1_out, or_2_out;
  wire [15:0] multiplexer_1_out, multiplexer_2_out, register_1_p1, undriven;

  Inc16 inc16_1 (.in(out));  // open: out
  or or_1 (or_1_out, load, reset);
  or or_2 (or_2_out, inc, or_1_out);
  Delay #(.delayTime(10)) delay_1 (.in(clk), .out(delay_1_out));
  // Register register_1: pin names not known; wires that end beside it: register_1_p1, or_2_out, delay_1_out
  Multiplexer #(.Bits(16)) multiplexer_1 (.sel(inc), .in_0(in), .in_1(undriven), .out(multiplexer_1_out));
  Multiplexer #(.Bits(16)) multiplexer_2 (.sel(load), .in_0(multiplexer_1_out), .in_1(in), .out(multiplexer_2_out));
  Multiplexer #(.Bits(16)) multiplexer_3 (
    .sel(reset), .in_0(multiplexer_2_out), .in_1({16{1'b0}}), .out(register_1_p1));
endmodule
