// Digital circuit Bit.dig as structural Verilog
module Bit (
  input  load,
  input  in,
  input  clk,
  output out
);

  wire multiplexer_1_out;

  Multiplexer multiplexer_1 (.sel(load), .in_0(out), .in_1(in), .out(multiplexer_1_out));
  DFF dff_1 (.in(multiplexer_1_out), .clk(clk));  // open: out
endmodule
