// Digital circuit DeviceCtrl.dig as structural Verilog
module DeviceCtrl (
  input  [3:0] device_submit,
  input  clk,
  input  enable,
  output [3:0] device_release,
  output device_commit
);

  wire and_1_out, dff_2_p3, not_1_out;

  and and_1 (and_1_out, enable, device_submit[0]);
  // DFF dff_1: pin names not known; wires that end beside it: and_1_out, clk, device_release
  // DFF dff_2: pin names not known; wires that end beside it: device_release, clk, dff_2_p3
  not not_1 (not_1_out, device_release[0]);
  and and_2 (device_commit, not_1_out, dff_2_p3);
  // Pins of 1 and 4 bits meet at device_submit
  // Pins of 1 and 4 bits meet at device_release
endmodule
