// Digital circuit RAM512.dig as structural Verilog
module RAM512 (
  input  [15:0] in,
  input  load,
  input  [8:0] address,
  input  clk,
  output [15:0] out
);

  wire demultiplexer_1_out_0, demultiplexer_1_out_1, demultiplexer_1_out_2, demultiplexer_1_out_3,
       demultiplexer_1_out_4, demultiplexer_1_out_5, demultiplexer_1_out_6, demultiplexer_1_out_7;
  wire [15:0] undriven, undriven_2, undriven_3, undriven_4, undriven_5, undriven_6, undriven_7, undriven_8;

  Demultiplexer #(.Selector_Bits(3)) demultiplexer_1 (
    .sel(address[8:6]), .in(load), .out_0(demultiplexer_1_out_0), .out_1(demultiplexer_1_out_1),
    .out_2(demultiplexer_1_out_2), .out_3(demultiplexer_1_out_3), .out_4(demultiplexer_1_out_4),
    .out_5(demultiplexer_1_out_5), .out_6(demultiplexer_1_out_6), .out_7(demultiplexer_1_out_7));
  RAM64 ram64_1 (.in(in), .load(demultiplexer_1_out_0), .address(address[5:0]), .clk(clk));  // open: out
  RAM64 ram64_2 (.in(in), .load(demultiplexer_1_out_2), .address(address[5:0]), .clk(clk));  // open: out
  RAM64 ram64_3 (.in(in), .load(demultiplexer_1_out_4), .address(address[5:0]), .clk(clk));  // open: out
  RAM64 ram64_4 (.in(in), .load(demultiplexer_1_out_6), .address(address[5:0]), .clk(clk));  // open: out
  RAM64 ram64_5 (.in(in), .load(demultiplexer_1_out_1), .address(address[5:0]), .clk(clk));  // open: out
  RAM64 ram64_6 (.in(in), .load(demultiplexer_1_out_3), .address(address[5:0]), .clk(clk));  // open: out
  RAM64 ram64_7 (.in(in), .load(demultiplexer_1_out_5), .address(address[5:0]), .clk(clk));  // open: out
  RAM64 ram64_8 (.in(in), .load(demultiplexer_1_out_7), .address(address[5:0]), .clk(clk));  // open: out
  Multiplexer #(.Selector_Bits(3), .Bits(16)) multiplexer_1 (
    .sel(address[8:6]), .in_0(undriven_7), .in_1(undriven_8), .in_2(undriven_6), .in_3(undriven_5),
    .in_4(undriven_4), .in_5(undriven_3), .in_6(undriven_2), .in_7(undriven), .out(out));
endmodule
