// Digital circuit RAM64.dig as structural Verilog
module RAM64 (
  input  [15:0] in,
  input  load,
  input  [5:0] address,
  input  clk,
  output [15:0] out
);

  wire demultiplexer_1_out_0, demultiplexer_1_out_1, demultiplexer_1_out_2, demultiplexer_1_out_3,
       demultiplexer_1_out_4, demultiplexer_1_out_5, demultiplexer_1_out_6, demultiplexer_1_out_7;
  wire [15:0] undriven, undriven_2, undriven_3, undriven_4, undriven_5, undriven_6, undriven_7, undriven_8;

  Demultiplexer #(.Selector_Bits(3)) demultiplexer_1 (
    .sel(address[5:3]), .in(load), .out_0(demultiplexer_1_out_0), .out_1(demultiplexer_1_out_1),
    .out_2(demultiplexer_1_out_2), .out_3(demultiplexer_1_out_3), .out_4(demultiplexer_1_out_4),
    .out_5(demultiplexer_1_out_5), .out_6(demultiplexer_1_out_6), .out_7(demultiplexer_1_out_7));
  // RAM8 ram8_1: pin names not known; wires that end beside it: in, demultiplexer_1_out_0, address[2:0], clk
  // RAM8 ram8_2: pin names not known; wires that end beside it: in, demultiplexer_1_out_2, address[2:0], clk
  // RAM8 ram8_3: pin names not known; wires that end beside it: in, demultiplexer_1_out_4, address[2:0], clk
  // RAM8 ram8_4: pin names not known; wires that end beside it: in, demultiplexer_1_out_6, address[2:0], clk
  // RAM8 ram8_5: pin names not known; wires that end beside it: in, demultiplexer_1_out_1, address[2:0], clk
  // RAM8 ram8_6: pin names not known; wires that end beside it: in, demultiplexer_1_out_3, address[2:0], clk
  // RAM8 ram8_7: pin names not known; wires that end beside it: in, demultiplexer_1_out_5, address[2:0], clk
  // RAM8 ram8_8: pin names not known; wires that end beside it: in, demultiplexer_1_out_7, address[2:0], clk
  Multiplexer #(.Selector_Bits(3), .Bits(16)) multiplexer_1 (
    .sel(address[5:3]), .in_0(undriven_8), .in_1(undriven_5), .in_2(undriven_4), .in_3(undriven_3),
    .in_4(undriven_7), .in_5(undriven_2), .in_6(undriven_6), .in_7(undriven), .out(out));
endmodule
