// Digital circuit Register.dig as structural Verilog
module Register (
  input  load,
  input  [15:0] in,
  input  clk,
  output [15:0] out
);

  // Bit bit_1: pin names not known; wires that end beside it: in[8], load, clk, out[8]
  // Bit bit_2: pin names not known; wires that end beside it: in[9], load, clk, out[9]
  // Bit bit_3: pin names not known; wires that end beside it: in[10], load, clk, out[10]
  // Bit bit_4: pin names not known; wires that end beside it: in[11], load, clk, out[11]
  // Bit bit_5: pin names not known; wires that end beside it: in[12], load, clk, out[12]
  // Bit bit_6: pin names not known; wires that end beside it: in[13], load, clk, out[13]
  // Bit bit_7: pin names not known; wires that end beside it: in[14], load, clk, out[14]
  // Bit bit_8: pin names not known; wires that end beside it: in[15], load, clk, out[15]
  // Bit bit_9: pin names not known; wires that end beside it: in[0], load, clk, out[0]
  // Bit bit_10: pin names not known; wires that end beside it: in[1], load, clk, out[1]
  // Bit bit_11: pin names not known; wires that end beside it: in[2], load, clk, out[2]
  // Bit bit_12: pin names not known; wires that end beside it: in[3], load, clk, out[3]
  // Bit bit_13: pin names not known; wires that end beside it: in[4], load, clk, out[4]
  // Bit bit_14: pin names not known; wires that end beside it: in[5], load, clk, out[5]
  // Bit bit_15: pin names not known; wires that end beside it: in[6], load, clk, out[6]
  // Bit bit_16: pin names not known; wires that end beside it: in[7], load, clk, out[7]
endmodule

/* Test case Test Load off:
        in         load clk         out
0b0000000000000000 0    0    0b0000000000000000
0b0000000000000000 0    C    0b0000000000000000
0b1111111111111111 0    0    0b0000000000000000
0b1111111111111111 0    C    0b0000000000000000
*/

/* Test case Test Load On:
        in         load clk         out
0b0000000000000001 0    C    0b0000000000000000
0b0000000000000001 1    C    0b0000000000000001
0b0000000000000010 0    C    0b0000000000000001
0b0000000000000010 1    C    0b0000000000000010
0b0000000000000100 0    C    0b0000000000000010
0b0000000000000100 1    C    0b0000000000000100
0b0000000000001000 0    C    0b0000000000000100
0b0000000000001000 1    C    0b0000000000001000
0b0000000000010000 0    C    0b0000000000001000
0b0000000000010000 1    C    0b0000000000010000
0b0000000000100000 0    C    0b0000000000010000
0b0000000000100000 1    C    0b0000000000100000
0b0000000001000000 0    C    0b0000000000100000
0b0000000001000000 1    C    0b0000000001000000
0b0000000010000000 0    C    0b0000000001000000
0b0000000010000000 1    C    0b0000000010000000
0b0000000100000000 0    C    0b0000000010000000
0b0000000100000000 1    C    0b0000000100000000
0b0000001000000000 0    C    0b0000000100000000
0b0000001000000000 1    C    0b0000001000000000
0b0000010000000000 0    C    0b0000001000000000
0b0000010000000000 1    C    0b0000010000000000
0b0000100000000000 0    C    0b0000010000000000
0b0000100000000000 1    C    0b0000100000000000
0b0001000000000000 0    C    0b0000100000000000
0b0001000000000000 1    C    0b0001000000000000
0b0010000000000000 0    C    0b0001000000000000
0b0010000000000000 1    C    0b0010000000000000
0b0100000000000000 0    C    0b0010000000000000
0b0100000000000000 1    C    0b0100000000000000
0b1000000000000000 0    C    0b0100000000000000
0b1000000000000000 1    C    0b1000000000000000
*/
