// Digital circuit test.dig as structural Verilog
module test (
  input  in_1,
  input  in_2,
  input  in_3,
  input  in_4,
  input  [2:0] in_5,
  input  in_6,
  input  [15:0] in_7,
  input  [15:0] in_8,
  output [15:0] out_9,
  output out_10,
  output out_11
);

  ALU alu_1 (
    .zx(in_1), .nx(in_2), .zy(in_3), .ny(in_4), .f(in_5), .no(in_6), .x(in_7), .y(in_8), .out(out_9),
    .ng(out_10), .zr(out_11));
endmodule
