// Digital circuit InputDecoder.dig as structural Verilog
module InputDecoder (
  input  [15:0] D,
  input  [15:0] A,
  input  [15:0] M,
  input  memory,
  input  [1:0] \input ,
  output [15:0] out
);

  wire [15:0] multiplexer_1_out;

  Multiplexer #(.Bits(16)) multiplexer_1 (.sel(memory), .in_0(A), .in_1(M), .out(multiplexer_1_out));
  Multiplexer #(.Selector_Bits(2), .Bits(16)) multiplexer_2 (
    .sel(\input ), .in_0(16'h1), .in_1(16'h2), .in_2(D), .in_3(multiplexer_1_out), .out(out));
endmodule
