// Digital circuit Memory.dig as structural Verilog
module Memory (
  input  [15:0] in,
  input  load,
  input  [14:0] address,
  input  clk,
  input  [63:0] device_in,
  input  [3:0] device_submit,
  output [3:0] device_release,
  output [15:0] out,
  output intok,
  output [63:0] device_out_0_3,
  output [63:0] device_out_4_7,
  output [63:0] device_out_8_11
);

  wire demultiplexer_1_out_0, demultiplexer_1_out_1, demultiplexer_2_out_0, demultiplexer_3_out_0,
       demultiplexer_4_out_0, demultiplexer_5_out_0, demultiplexer_6_out_1, demultiplexer_6_out_2,
       demultiplexer_6_out_3, devicectrl_1_p7, not_1_out, ram4transparent_1_p1;
  wire [15:0] devicectrl_1_p6, multiplexer_1_out, multiplexer_2_out, multiplexer_3_out, multiplexer_4_out,
       multiplexer_5_out, ram16k_1_out, undriven, undriven_2, undriven_3;

  Demultiplexer demultiplexer_1 (
    .sel(address[14]), .in(load), .out_0(demultiplexer_1_out_0), .out_1(demultiplexer_1_out_1));
  Interruptor interruptor_1 (.address(address));  // open: interrupt
  RAM16K ram16k_1 (.in(in), .load(demultiplexer_1_out_0), .address(address[13:0]), .clk(clk), .out(ram16k_1_out));
  Demultiplexer #(.Selector_Bits(2)) demultiplexer_2 (
    .sel(address[13:12]), .in(demultiplexer_1_out_1), .out_0(demultiplexer_2_out_0));  // open: out_1, out_2, out_3
  Demultiplexer #(.Selector_Bits(3)) demultiplexer_3 (
    .sel(address[11:9]), .in(demultiplexer_2_out_0), .out_0(demultiplexer_3_out_0));  // open: out_1, out_2, out_3, out_4, out_5, out_6, out_7
  Demultiplexer #(.Selector_Bits(3)) demultiplexer_4 (
    .sel(address[8:6]), .in(demultiplexer_3_out_0), .out_0(demultiplexer_4_out_0));  // open: out_1, out_2, out_3, out_4, out_5, out_6, out_7
  Demultiplexer #(.Selector_Bits(2)) demultiplexer_5 (
    .sel(address[5:4]), .in(demultiplexer_4_out_0), .out_0(demultiplexer_5_out_0));  // open: out_1, out_2, out_3
  Demultiplexer #(.Selector_Bits(2)) demultiplexer_6 (
    .sel(address[3:2]), .in(demultiplexer_5_out_0), .out_1(demultiplexer_6_out_1),
    .out_2(demultiplexer_6_out_2), .out_3(demultiplexer_6_out_3));  // open: out_0
  // RAM4Transparent ram4transparent_1: pin names not known; wires that end beside it: ram4transparent_1_p1, in, demultiplexer_6_out_1, address[1:0], clk
  // RAM4Transparent ram4transparent_2: pin names not known; wires that end beside it: in, demultiplexer_6_out_2, address[1:0], clk
  // RAM4Transparent ram4transparent_3: pin names not known; wires that end beside it: in, demultiplexer_6_out_3, address[1:0], clk
  // DeviceCtrl devicectrl_1: pin names not known; wires that end beside it: address[1:0], clk, address[14], device_in, device_submit, devicectrl_1_p6, devicectrl_1_p7, device_release
  not not_1 (not_1_out, ram4transparent_1_p1);
  or or_1 (intok, not_1_out, devicectrl_1_p7);
  Multiplexer #(.Selector_Bits(2), .Bits(16)) multiplexer_1 (
    .sel(address[3:2]), .in_0(devicectrl_1_p6), .in_1(undriven), .in_2(undriven_2), .in_3(undriven_3),
    .out(multiplexer_1_out));
  Multiplexer #(.Selector_Bits(2), .Bits(16)) multiplexer_2 (
    .sel(address[5:4]), .in_0(multiplexer_1_out), .in_1({16{1'b0}}), .in_2({16{1'b0}}), .in_3({16{1'b0}}),
    .out(multiplexer_2_out));
  Multiplexer #(.Selector_Bits(3), .Bits(16)) multiplexer_3 (
    .sel(address[8:6]), .in_0(multiplexer_2_out), .in_1({16{1'b0}}), .in_2({16{1'b0}}), .in_3({16{1'b0}}),
    .in_4({16{1'b0}}), .in_5({16{1'b0}}), .in_6({16{1'b0}}), .in_7({16{1'b0}}), .out(multiplexer_3_out));
  Multiplexer #(.Selector_Bits(3), .Bits(16)) multiplexer_4 (
    .sel(address[11:9]), .in_0(multiplexer_3_out), .in_1({16{1'b0}}), .in_2({16{1'b0}}), .in_3({16{1'b0}}),
    .in_4({16{1'b0}}), .in_5({16{1'b0}}), .in_6({16{1'b0}}), .in_7({16{1'b0}}), .out(multiplexer_4_out));
  Multiplexer #(.Selector_Bits(2), .Bits(16)) multiplexer_5 (
    .sel(address[13:12]), .in_0(multiplexer_4_out), .in_1({16{1'b0}}), .in_2({16{1'b0}}), .in_3({16{1'b0}}),
    .out(multiplexer_5_out));
  Multiplexer #(.Bits(16)) multiplexer_6 (.sel(address[14]), .in_0(ram16k_1_out), .in_1(multiplexer_5_out), .out(out));
endmodule
