// Digital circuit DFF.dig as structural Verilog
module DFF (
  input  in,
  input  clk,
  output out
);

  wire multiplexer_1_out, not_1_out;

  Multiplexer multiplexer_1 (.sel(not_1_out), .in_0(multiplexer_1_out), .in_1(in), .out(multiplexer_1_out));
  Multiplexer multiplexer_2 (.sel(clk), .in_0(out), .in_1(multiplexer_1_out), .out(out));
  not not_1 (not_1_out, clk);
endmodule
