// Digital circuit DeviceCtrl.dig as structural Verilog
module DeviceCtrl (
  input  [3:0] device_submit,
  input  [63:0] device_in,
  input  [1:0] address,
  input  clk,
  input  enable,
  output [3:0] device_release,
  output [15:0] out,
  output device_commit
);

  wire and_1_out, multiplexer_1_out, not_1_out, undriven, undriven_2;

  Multiplexer #(.Selector_Bits(2)) multiplexer_1 (
    .sel(address), .in_0(device_submit[0]), .in_1(device_submit[1]), .in_2(device_submit[2]),
    .in_3(device_submit[3]), .out(multiplexer_1_out));
  and and_1 (and_1_out, enable, multiplexer_1_out);
  Multiplexer #(.Selector_Bits(2), .Bits(16)) multiplexer_2 (
    .sel(address), .in_0(device_in[15:0]), .in_1(device_in[31:16]), .in_2(device_in[47:32]),
    .in_3(device_in[63:48]), .out(out));
  DFF dff_1 (.in(and_1_out), .clk(clk));  // open: out
  DFF dff_2 (.in(undriven), .clk(clk));  // open: out
  not not_1 (not_1_out, undriven);
  Demultiplexer #(.Selector_Bits(2)) demultiplexer_1 (
    .sel(address), .in(undriven), .out_0(device_release[0]), .out_1(device_release[1]),
    .out_2(device_release[2]), .out_3(device_release[3]));
  and and_2 (device_commit, not_1_out, undriven_2);
endmodule
