// Digital circuit Interruptor.dig as structural Verilog
module Interruptor (
  input  [14:0] address,
  output interrupt
);

  wire and_1_out, and_2_out, and_3_out, and_4_out, and_5_out, and_6_out, and_7_out, and_8_out, and_9_out,
       and_10_out, and_11_out, not_1_out, not_2_out, not_3_out, not_4_out, not_5_out, not_6_out, not_7_out,
       not_8_out, not_9_out, not_10_out, not_11_out, not_12_out, not_13_out, xor_1_out, xor_2_out, xor_3_out,
       xor_4_out, xor_5_out, xor_6_out, xor_7_out, xor_8_out, xor_9_out, xor_10_out, xor_11_out, xor_12_out,
       xor_13_out;

  xor xor_1 (xor_1_out, address[2], 1'b0);
  xor xor_2 (xor_2_out, address[3], 1'b0);
  xor xor_3 (xor_3_out, address[4], 1'b0);
  xor xor_4 (xor_4_out, address[5], 1'b0);
  xor xor_5 (xor_5_out, address[6], 1'b0);
  xor xor_6 (xor_6_out, address[7], 1'b0);
  xor xor_7 (xor_7_out, address[8], 1'b0);
  xor xor_8 (xor_8_out, address[9], 1'b0);
  xor xor_9 (xor_9_out, address[10], 1'b0);
  xor xor_10 (xor_10_out, address[11], 1'b0);
  xor xor_11 (xor_11_out, address[12], 1'b0);
  xor xor_12 (xor_12_out, address[13], 1'b0);
  xor xor_13 (xor_13_out, address[14], 1'b1);
  not not_1 (not_1_out, xor_1_out);
  not not_2 (not_2_out, xor_2_out);
  not not_3 (not_3_out, xor_3_out);
  not not_4 (not_4_out, xor_4_out);
  not not_5 (not_5_out, xor_5_out);
  not not_6 (not_6_out, xor_6_out);
  not not_7 (not_7_out, xor_7_out);
  not not_8 (not_8_out, xor_8_out);
  not not_9 (not_9_out, xor_9_out);
  not not_10 (not_10_out, xor_10_out);
  not not_11 (not_11_out, xor_11_out);
  not not_12 (not_12_out, xor_12_out);
  not not_13 (not_13_out, xor_13_out);
  and and_1 (and_1_out, not_2_out, not_3_out);
  and and_2 (and_2_out, not_4_out, not_5_out);
  and and_3 (and_3_out, not_6_out, not_7_out);
  and and_4 (and_4_out, not_8_out, not_9_out);
  and and_5 (and_5_out, not_10_out, not_11_out);
  and and_6 (and_6_out, not_12_out, not_13_out);
  and and_7 (and_7_out, and_1_out, and_2_out);
  and and_8 (and_8_out, and_3_out, and_4_out);
  and and_9 (and_9_out, and_5_out, and_6_out);
  and and_10 (and_10_out, not_1_out, and_7_out);
  and and_11 (and_11_out, and_8_out, and_9_out);
  and and_12 (interrupt, and_10_out, and_11_out);

  // Notes on the sheet:
  //   DEV IN addresses
  //   0b100000000000000
  //   0b100000000000001
  //   0b100000000000010
  //   0b100000000000011
endmodule
