// Digital circuit RAM16K.dig as structural Verilog
module RAM16K (
  input  [15:0] in,
  input  load,
  input  [13:0] address,
  input  clk,
  output [15:0] out
);

  wire demultiplexer_1_out_0, demultiplexer_1_out_1, demultiplexer_1_out_2, demultiplexer_1_out_3;
  wire [15:0] undriven, undriven_2, undriven_3, undriven_4;

  Demultiplexer #(.Selector_Bits(2)) demultiplexer_1 (
    .sel(address[13:12]), .in(load), .out_0(demultiplexer_1_out_0), .out_1(demultiplexer_1_out_1),
    .out_2(demultiplexer_1_out_2), .out_3(demultiplexer_1_out_3));
  RAM4K ram4k_1 (.in(in), .load(demultiplexer_1_out_3), .address(address[11:0]), .clk(clk));  // open: out
  RAM4K ram4k_2 (.in(in), .load(demultiplexer_1_out_2), .address(address[11:0]), .clk(clk));  // open: out
  RAM4K ram4k_3 (.in(in), .load(demultiplexer_1_out_1), .address(address[11:0]), .clk(clk));  // open: out
  RAM4K ram4k_4 (.in(in), .load(demultiplexer_1_out_0), .address(address[11:0]), .clk(clk));  // open: out
  Multiplexer #(.Selector_Bits(2), .Bits(16)) multiplexer_1 (
    .sel(address[13:12]), .in_0(undriven), .in_1(undriven_2), .in_2(undriven_3), .in_3(undriven_4), .out(out));
endmodule
