// Digital circuit RAM4Transparent.dig as structural Verilog
module RAM4Transparent (
  input  load,
  input  [15:0] in,
  input  clk,
  input  [1:0] address,
  output [15:0] out,
  output [63:0] out_transparent
);

  wire demultiplexer_1_out_0, demultiplexer_1_out_1, demultiplexer_1_out_2, demultiplexer_1_out_3;

  Demultiplexer #(.Selector_Bits(2)) demultiplexer_1 (
    .sel(address), .in(load), .out_0(demultiplexer_1_out_0), .out_1(demultiplexer_1_out_1),
    .out_2(demultiplexer_1_out_2), .out_3(demultiplexer_1_out_3));
  // Register register_1: pin names not known; wires that end beside it: in, demultiplexer_1_out_0, clk
  // Register register_2: pin names not known; wires that end beside it: in, demultiplexer_1_out_2, clk
  // Register register_3: pin names not known; wires that end beside it: in, demultiplexer_1_out_1, clk
  // Register register_4: pin names not known; wires that end beside it: out_transparent[15:0], in, demultiplexer_1_out_3, clk
  Multiplexer #(.Selector_Bits(2), .Bits(16)) multiplexer_1 (
    .sel(address), .in_0(out_transparent[15:0]), .in_1(out_transparent[31:16]),
    .in_2(out_transparent[47:32]), .in_3(out_transparent[63:48]), .out(out));
endmodule
