// Digital circuit RAM8.dig as structural Verilog
module RAM8 (
  input  load,
  input  [15:0] in,
  input  clk,
  input  [2:0] address,
  output [15:0] out
);

  wire demultiplexer_1_out_0, demultiplexer_1_out_1, demultiplexer_1_out_2, demultiplexer_1_out_3,
       demultiplexer_1_out_4, demultiplexer_1_out_5, demultiplexer_1_out_6, demultiplexer_1_out_7;
  wire [15:0] register_6_p1, register_7_p1, register_8_p1, undriven, undriven_2, undriven_3, undriven_4,
       undriven_5;

  Demultiplexer #(.Selector_Bits(3)) demultiplexer_1 (
    .sel(address), .in(load), .out_0(demultiplexer_1_out_0), .out_1(demultiplexer_1_out_1),
    .out_2(demultiplexer_1_out_2), .out_3(demultiplexer_1_out_3), .out_4(demultiplexer_1_out_4),
    .out_5(demultiplexer_1_out_5), .out_6(demultiplexer_1_out_6), .out_7(demultiplexer_1_out_7));
  // Register register_1: pin names not known; wires that end beside it: in, demultiplexer_1_out_0, clk
  // Register register_2: pin names not known; wires that end beside it: in, demultiplexer_1_out_2, clk
  // Register register_3: pin names not known; wires that end beside it: in, demultiplexer_1_out_4, clk
  // Register register_4: pin names not known; wires that end beside it: in, demultiplexer_1_out_6, clk
  // Register register_5: pin names not known; wires that end beside it: in, demultiplexer_1_out_1, clk
  // Register register_6: pin names not known; wires that end beside it: register_6_p1, in, demultiplexer_1_out_3, clk
  // Register register_7: pin names not known; wires that end beside it: register_7_p1, in, demultiplexer_1_out_5, clk
  // Register register_8: pin names not known; wires that end beside it: register_8_p1, in, demultiplexer_1_out_7, clk
  Multiplexer #(.Selector_Bits(3), .Bits(16)) multiplexer_1 (
    .sel(address), .in_0(register_6_p1), .in_1(undriven_5), .in_2(register_7_p1), .in_3(undriven_4),
    .in_4(register_8_p1), .in_5(undriven_3), .in_6(undriven_2), .in_7(undriven), .out(out));
endmodule

/* Test case Test all cells:
        in         load clk address         out
0b0000000000000001 1    C   0       0b0000000000000001
0b0000000000000001 0    0   1       0b0000000000000000
0b0000000000000001 0    0   2       0b0000000000000000
0b0000000000000001 0    0   3       0b0000000000000000
0b0000000000000001 0    0   4       0b0000000000000000
0b0000000000000001 0    0   5       0b0000000000000000
0b0000000000000001 0    0   6       0b0000000000000000
0b0000000000000001 0    0   7       0b0000000000000000
0b0000000000000000 1    C   0       0b0000000000000000

0b0000000000000001 1    C   1       0b0000000000000001
0b0000000000000001 0    0   0       0b0000000000000000
0b0000000000000001 0    0   2       0b0000000000000000
0b0000000000000001 0    0   3       0b0000000000000000
0b0000000000000001 0    0   4       0b0000000000000000
0b0000000000000001 0    0   5       0b0000000000000000
0b0000000000000001 0    0   6       0b0000000000000000
0b0000000000000001 0    0   7       0b0000000000000000
0b0000000000000000 1    C   1       0b0000000000000000

0b0000000000000001 1    C   2       0b0000000000000001
0b0000000000000001 0    0   0       0b0000000000000000
0b0000000000000001 0    0   1       0b0000000000000000
0b0000000000000001 0    0   3       0b0000000000000000
0b0000000000000001 0    0   4       0b0000000000000000
0b0000000000000001 0    0   5       0b0000000000000000
0b0000000000000001 0    0   6       0b0000000000000000
0b0000000000000001 0    0   7       0b0000000000000000
0b0000000000000000 1    C   2       0b0000000000000000

0b0000000000000001 1    C   3       0b0000000000000001
0b0000000000000001 0    0   0       0b0000000000000000
0b0000000000000001 0    0   1       0b0000000000000000
0b0000000000000001 0    0   2       0b0000000000000000
0b0000000000000001 0    0   4       0b0000000000000000
0b0000000000000001 0    0   5       0b0000000000000000
0b0000000000000001 0    0   6       0b0000000000000000
0b0000000000000001 0    0   7       0b0000000000000000
0b0000000000000000 1    C   3       0b0000000000000000

0b0000000000000001 1    C   4       0b0000000000000001
0b0000000000000001 0    0   0       0b0000000000000000
0b0000000000000001 0    0   1       0b0000000000000000
0b0000000000000001 0    0   2       0b0000000000000000
0b0000000000000001 0    0   3       0b0000000000000000
0b0000000000000001 0    0   5       0b0000000000000000
0b0000000000000001 0    0   6       0b0000000000000000
0b0000000000000001 0    0   7       0b0000000000000000
0b0000000000000000 1    C   4       0b0000000000000000

0b0000000000000001 1    C   5       0b0000000000000001
0b0000000000000001 0    0   0       0b0000000000000000
0b0000000000000001 0    0   1       0b0000000000000000
0b0000000000000001 0    0   2       0b0000000000000000
0b0000000000000001 0    0   3       0b0000000000000000
0b0000000000000001 0    0   4       0b0000000000000000
0b0000000000000001 0    0   6       0b0000000000000000
0b0000000000000001 0    0   7       0b0000000000000000
0b0000000000000000 1    C   5       0b0000000000000000

0b0000000000000001 1    C   6       0b0000000000000001
0b0000000000000001 0    0   0       0b0000000000000000
0b0000000000000001 0    0   1       0b0000000000000000
0b0000000000000001 0    0   2       0b0000000000000000
0b0000000000000001 0    0   3       0b0000000000000000
0b0000000000000001 0    0   4       0b0000000000000000
0b0000000000000001 0    0   5       0b0000000000000000
0b0000000000000001 0    0   7       0b0000000000000000
0b0000000000000000 1    C   6       0b0000000000000000

0b0000000000000001 1    C   7       0b0000000000000001
0b0000000000000001 0    0   0       0b0000000000000000
0b0000000000000001 0    0   1       0b0000000000000000
0b0000000000000001 0    0   2       0b0000000000000000
0b0000000000000001 0    0   3       0b0000000000000000
0b0000000000000001 0    0   4       0b0000000000000000
0b0000000000000001 0    0   5       0b0000000000000000
0b0000000000000001 0    0   6       0b0000000000000000
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*/
